# Fritzing sketch iot-arduino-rtos-queue-01 (saved by Fritzing 0.9.9b)
breadboards: 1

parts:
  Bauteil1 = Arduino Uno (Rev3)
  LED1 = LED - 5mm [color="Red (633nm)" current=0.030 package="5 mm [THT]"]
  LED2 = LED - 5mm [color="Yellow (595nm)" current=0.030 package="5 mm [THT]"]
  R5 = Resistor [tolerance=±5% power=0.25 resistance=560 package=THT]
  R6 = Resistor [tolerance=±5% power=0.25 resistance=560 package=THT]
  R7 = Trimmer Potentiometer [maximum_resistance=10kΩ package=THT]
  R8 = Trimmer Potentiometer [maximum_resistance=10kΩ package=THT]
  C5 = Ceramic Capacitor [capacitance=100nF voltage=35V package="100 mil [THT, multilayer]"]

nets:
  N1: Bauteil1.A0, R7.wiper
  N2: Bauteil1.A1, R8.wiper
  N3: Bauteil1.A2, Bauteil1.3V3, R7.leg2, R8.leg2, C5.1
  N4: Bauteil1.D11_PWM/MOSI, LED2.anode
  N5: Bauteil1.D12/MISO, LED1.anode
  N6: Bauteil1.GND, R5.Pin_1, R6.Pin_1, R7.leg1, R8.leg1, C5.0
  N7: LED1.cathode, R6.Pin_0
  N8: LED2.cathode, R5.Pin_0

notes:
  iot-arduino-rtos-queue-01
  rot
  gelb
